// Digital circuit 74181_noPower.dig as structural Verilog
// 4-bit arithmetic logic unit (no power pins)
module _74181_noPower (
  input  Cn,
  input  nA0,
  input  nA1,
  input  nA2,
  input  nA3,
  input  nB0,
  input  nB1,
  input  nB2,
  input  nB3,
  input  S0,
  input  S1,
  input  S2,
  input  S3,
  input  M,
  output nG,
  output nP,
  output nF0,
  output nF1,
  output nF2,
  output nF3,
  output A_eq_B,
  output Cn_plus_4
);

  wire and_1_out, and_2_out, and_3_out, and_4_out, and_5_out, and_6_out, and_7_out, and_8_out, and_9_out,
       and_10_out, and_11_out, and_12_out, and_13_out, and_14_out, and_15_out, and_16_out, and_17_out,
       and_18_out, and_19_out, and_20_out, and_21_out, and_22_out, and_23_out, and_24_out, and_25_out,
       and_26_out, and_27_out, and_28_out, and_29_out, and_30_out, and_31_out, and_32_out, nand_1_out,
       nand_3_out, nor_1_out, nor_2_out, nor_3_out, nor_4_out, nor_5_out, nor_6_out, nor_7_out, nor_8_out,
       nor_10_out, nor_11_out, nor_12_out, not_1_out, not_2_out, not_3_out, not_4_out, not_5_out, not_6_out,
       not_7_out, not_8_out, not_9_out;

  not not_1 (not_1_out, nB3);
  not not_2 (not_2_out, nB2);
  not not_3 (not_3_out, nB1);
  not not_4 (not_4_out, nB0);
  not not_5 (not_5_out, M);
  and and_1 (and_1_out, S3, nB3, nA3);
  and and_2 (and_2_out, nA3, S2, not_1_out);
  and and_3 (and_3_out, not_1_out, S1);
  and and_4 (and_4_out, S0, nB3);
  and and_5 (and_5_out, nB2, S3, nA2);
  and and_6 (and_6_out, nA2, S2, not_2_out);
  and and_7 (and_7_out, not_2_out, S1);
  and and_8 (and_8_out, S0, nB2);
  and and_9 (and_9_out, nB1, S3, nA1);
  and and_10 (and_10_out, nA1, S2, not_3_out);
  and and_11 (and_11_out, not_3_out, S1);
  and and_12 (and_12_out, S0, nB1);
  and and_13 (and_13_out, S3, nB0, nA0);
  and and_14 (and_14_out, nA0, S2, not_4_out);
  and and_15 (and_15_out, not_4_out, S1);
  and and_16 (and_16_out, S0, nB0);
  nor nor_1 (nor_1_out, and_1_out, and_2_out);
  nor nor_2 (nor_2_out, and_3_out, and_4_out, nA3);
  nor nor_3 (nor_3_out, and_5_out, and_6_out);
  nor nor_4 (nor_4_out, and_7_out, and_8_out, nA2);
  nor nor_5 (nor_5_out, and_9_out, and_10_out);
  nor nor_6 (nor_6_out, and_11_out, and_12_out, nA1);
  nor nor_7 (nor_7_out, and_13_out, and_14_out);
  nor nor_8 (nor_8_out, and_15_out, and_16_out, nA0);
  and and_17 (and_17_out, nor_1_out, nor_4_out);
  and and_18 (and_18_out, nor_1_out, nor_3_out, nor_6_out);
  and and_19 (and_19_out, nor_1_out, nor_3_out, nor_5_out, nor_8_out);
  nand nand_1 (nand_1_out, nor_1_out, nor_3_out, nor_5_out, nor_7_out, Cn);
  nand nand_2 (nP, nor_1_out, nor_3_out, nor_5_out, nor_7_out);
  not not_6 (not_6_out, nor_2_out);
  and and_20 (and_20_out, nor_3_out, nor_5_out, nor_7_out, Cn, not_5_out);
  and and_21 (and_21_out, nor_3_out, nor_5_out, nor_8_out, not_5_out);
  and and_22 (and_22_out, nor_3_out, nor_6_out, not_5_out);
  and and_23 (and_23_out, nor_4_out, not_5_out);
  not not_7 (not_7_out, nor_4_out);
  and and_24 (and_24_out, nor_5_out, nor_7_out, Cn, not_5_out);
  and and_25 (and_25_out, nor_5_out, nor_8_out, not_5_out);
  and and_26 (and_26_out, nor_6_out, not_5_out);
  not not_8 (not_8_out, nor_6_out);
  and and_27 (and_27_out, Cn, nor_7_out, not_5_out);
  and and_28 (and_28_out, nor_8_out, not_5_out);
  not not_9 (not_9_out, nor_8_out);
  nand nand_3 (nand_3_out, not_5_out, Cn);
  nor nor_9 (nG, nor_2_out, and_17_out, and_18_out, and_19_out);
  and and_29 (and_29_out, nor_1_out, not_6_out);
  nor nor_10 (nor_10_out, and_20_out, and_21_out, and_22_out, and_23_out);
  and and_30 (and_30_out, nor_3_out, not_7_out);
  nor nor_11 (nor_11_out, and_24_out, and_25_out, and_26_out);
  and and_31 (and_31_out, nor_5_out, not_8_out);
  nor nor_12 (nor_12_out, and_27_out, and_28_out);
  and and_32 (and_32_out, nor_7_out, not_9_out);
  nand nand_4 (Cn_plus_4, nG, nand_1_out);
  xor xor_1 (nF3, and_29_out, nor_10_out);
  xor xor_2 (nF2, and_30_out, nor_11_out);
  xor xor_3 (nF1, and_31_out, nor_12_out);
  xor xor_4 (nF0, and_32_out, nand_3_out);
  and and_33 (A_eq_B, nF3, nF2, nF1, nF0);

  // Notes on the sheet:
  //   Cn: pin 7
  //   nA0: pin 2
  //   nA1: pin 23
  //   nA2: pin 21
  //   nA3: pin 19
  //   nB0: pin 1
  //   nB1: pin 22
  //   nB2: pin 20
  //   nB3: pin 18
  //   S0: pin 6
  //   S1: pin 5
  //   S2: pin 4
  //   S3: pin 3
  //   M: pin 8
  //   nG: pin 17
  //   nP: pin 15
  //   nF0: pin 9
  //   nF1: pin 10
  //   nF2: pin 11
  //   nF3: pin 13
  //   A_eq_B: pin 14
  //   Cn_plus_4: pin 16
  //   Logic Tests
  //       (M=1)
  //   Arithmetic Tests
  //     (M=0, Cn=1)
endmodule
