// Digital circuit 74283_noPower.dig as structural Verilog
// 4-bit binary full adder, alternative pinning (no power pins)
module _74283_noPower (
  input  C0,
  input  B1,
  input  B2,
  input  B3,
  input  B4,
  input  A1,
  input  A2,
  input  A3,
  input  A4,
  output S1,
  output S2,
  output S3,
  output S4,
  output C4
);

  Add #(.Bits(4)) add_1 (.a({A4, A3, A2, A1}), .b({B4, B3, B2, B1}), .c_i(C0), .s({S4, S3, S2, S1}), .c_o(C4));

  // Notes on the sheet:
  //   C0: pin 7
  //   B1: pin 6
  //   B2: pin 2
  //   S1: pin 4
  //   B3: pin 15
  //   B4: pin 11
  //   S2: pin 1
  //   S3: pin 13
  //   A1: pin 5
  //   A2: pin 3
  //   A3: pin 14
  //   A4: pin 12
  //   S4: pin 10
  //   C4: pin 9
endmodule
