// Digital circuit 7482_noPower.dig as structural Verilog
// 2-bit binary full adder (no power pins)
module _7482_noPower (
  input  C0,
  input  B1,
  input  B2,
  input  A1,
  input  A2,
  output S1,
  output S2,
  output C2
);

  Add #(.Bits(2)) add_1 (.a({A2, A1}), .b({B2, B1}), .c_i(C0), .s({S2, S1}), .c_o(C2));

  // Notes on the sheet:
  //   C0: pin 5
  //   B1: pin 3
  //   B2: pin 13
  //   S1: pin 1
  //   S2: pin 12
  //   A1: pin 2
  //   A2: pin 14
  //   C2: pin 10
endmodule
