// Digital circuit 7408_noPower.dig as structural Verilog
// quad 2-input AND gate (no power pins)
module _7408_noPower (
  input  _1A,
  input  _1B,
  input  _2A,
  input  _2B,
  input  _3B,
  input  _3A,
  input  _4A,
  input  _4B,
  output _1Y,
  output _2Y,
  output _3Y,
  output _4Y
);

  and and_1 (_1Y, _1A, _1B);
  and and_2 (_2Y, _2A, _2B);
  and and_3 (_3Y, _3A, _3B);
  and and_4 (_4Y, _4A, _4B);

  // Notes on the sheet:
  //   _1A: pin 1
  //   _1B: pin 2
  //   _1Y: pin 3
  //   _2A: pin 4
  //   _2B: pin 5
  //   _2Y: pin 6
  //   _3B: pin 10
  //   _3A: pin 9
  //   _3Y: pin 8
  //   _4A: pin 12
  //   _4B: pin 13
  //   _4Y: pin 11
endmodule
