// Digital circuit 74133_noPower.dig as structural Verilog
// 13-input NAND gate (no power pins)
module _74133_noPower (
  input  A,
  input  B,
  input  C,
  input  D,
  input  E,
  input  F,
  input  G,
  input  H,
  input  I,
  input  J,
  input  K,
  input  L,
  input  M,
  output Y
);

  nand nand_1 (Y, A, B, C, D, E, F, G, H, I, J, K, L, M);

  // Notes on the sheet:
  //   Y: pin 9
  //   A: pin 1
  //   B: pin 2
  //   C: pin 3
  //   D: pin 4
  //   E: pin 5
  //   F: pin 6
  //   G: pin 7
  //   H: pin 10
  //   I: pin 11
  //   J: pin 12
  //   K: pin 13
  //   L: pin 14
  //   M: pin 15
endmodule
