// Digital circuit 7415_noPower.dig as structural Verilog
// triple 3-input AND gate with open-collector outputs (no power pins)
module _7415_noPower (
  input  _1A,
  input  _1C,
  input  _2A,
  input  _2C,
  input  _3C,
  input  _3A,
  input  _1B,
  input  _2B,
  input  _3B,
  output _1Y,
  output _2Y,
  output _3Y
);

  wire nand_1_out, nand_2_out, nand_3_out;

  nand nand_1 (nand_1_out, _1A, _1B, _1C);
  nand nand_2 (nand_2_out, _2A, _2B, _2C);
  nand nand_3 (nand_3_out, _3A, _3B, _3C);
  NFET nfet_1 (.G(nand_1_out), .D(_1Y), .S(1'b0));
  NFET nfet_2 (.G(nand_2_out), .D(_2Y), .S(1'b0));
  NFET nfet_3 (.G(nand_3_out), .D(_3Y), .S(1'b0));

  // Notes on the sheet:
  //   _1A: pin 1
  //   _1C: pin 13
  //   _1Y: pin 12
  //   _2A: pin 3
  //   _2C: pin 5
  //   _2Y: pin 6
  //   _3C: pin 11
  //   _3A: pin 9
  //   _3Y: pin 8
  //   _1B: pin 2
  //   _2B: pin 4
  //   _3B: pin 10
endmodule
