// Digital circuit 7425_noPower.dig as structural Verilog
// dual 4-input NOR gate with strobe (no power pins)
module _7425_noPower (
  input  _1A,
  input  _1C,
  input  _2A,
  input  _2C,
  input  _1B,
  input  _2B,
  input  _1D,
  input  _2D,
  input  _1G,
  input  _2G,
  output _1Y,
  output _2Y
);

  wire or_1_out, or_2_out;

  or or_1 (or_1_out, _1A, _1B, _1C, _1D);
  or or_2 (or_2_out, _2A, _2B, _2C, _2D);
  nand nand_1 (_1Y, or_1_out, _1G);
  nand nand_2 (_2Y, or_2_out, _2G);

  // Notes on the sheet:
  //   _1A: pin 1
  //   _1C: pin 4
  //   _1Y: pin 6
  //   _2A: pin 9
  //   _2C: pin 12
  //   _2Y: pin 8
  //   _1B: pin 2
  //   _2B: pin 10
  //   _1D: pin 5
  //   _2D: pin 13
  //   _1G: pin 3
  //   _2G: pin 11
endmodule
