// Digital circuit 74260_noPower.dig as structural Verilog
// dual 5-input NOR gate (no power pins)
module _74260_noPower (
  input  _1A,
  input  _1B,
  input  _1C,
  input  _1D,
  input  _1E,
  input  _2A,
  input  _2B,
  input  _2C,
  input  _2D,
  input  _2E,
  output _1Y,
  output _2Y
);

  nor nor_1 (_1Y, _1A, _1B, _1C, _1D, _1E);
  nor nor_2 (_2Y, _2A, _2B, _2C, _2D, _2E);

  // Notes on the sheet:
  //   _1A: pin 1
  //   _1B: pin 2
  //   _1C: pin 3
  //   _1D: pin 12
  //   _1E: pin 13
  //   _1Y: pin 5
  //   _2A: pin 4
  //   _2B: pin 11
  //   _2C: pin 10
  //   _2D: pin 9
  //   _2E: pin 8
  //   _2Y: pin 6
endmodule
