// Digital circuit 7430_noPower.dig as structural Verilog
// 8-input NAND gate (no power pins)
module _7430_noPower (
  input  _1A,
  input  _1C,
  input  _1B,
  input  _1D,
  input  _1E,
  input  _1G,
  input  _1F,
  input  _1H,
  output _1Y
);

  nand nand_1 (_1Y, _1A, _1B, _1C, _1D, _1E, _1F, _1G, _1H);

  // Notes on the sheet:
  //   _1A: pin 1
  //   _1C: pin 3
  //   _1Y: pin 8
  //   _1B: pin 2
  //   _1D: pin 4
  //   _1E: pin 5
  //   _1G: pin 11
  //   _1F: pin 6
  //   _1H: pin 12
endmodule
