// Digital circuit 744002_noPower.dig as structural Verilog
// dual 4-input NOR gate (no power pins)
module _744002_noPower (
  input  _1A,
  input  _1B,
  input  _1C,
  input  _1D,
  input  _2B,
  input  _2A,
  input  _2C,
  input  _2D,
  output _1Y,
  output _2Y
);

  nor nor_1 (_1Y, _1A, _1B, _1C, _1D);
  nor nor_2 (_2Y, _2A, _2B, _2C, _2D);

  // Notes on the sheet:
  //   _1A: pin 2
  //   _1B: pin 3
  //   _1Y: pin 1
  //   _1C: pin 4
  //   _1D: pin 5
  //   _2B: pin 10
  //   _2A: pin 9
  //   _2C: pin 11
  //   _2D: pin 12
  //   _2Y: pin 13
endmodule
