// Digital circuit 744075_noPower.dig as structural Verilog
// triple 3-input OR gate (no power pins)
module _744075_noPower (
  input  _1A,
  input  _1C,
  input  _1B,
  input  _2A,
  input  _2C,
  input  _2B,
  input  _3A,
  input  _3C,
  input  _3B,
  output _1Y,
  output _2Y,
  output _3Y
);

  or or_1 (_1Y, _1A, _1B, _1C);
  or or_2 (_2Y, _2A, _2B, _2C);
  or or_3 (_3Y, _3A, _3B, _3C);

  // Notes on the sheet:
  //   _1Y: pin 9
  //   _1A: pin 1
  //   _1C: pin 8
  //   _1B: pin 2
  //   _2Y: pin 6
  //   _2A: pin 3
  //   _2C: pin 5
  //   _2B: pin 4
  //   _3Y: pin 10
  //   _3A: pin 11
  //   _3C: pin 13
  //   _3B: pin 12
endmodule
