// Digital circuit 7455_noPower.dig as structural Verilog
// 2 wide 4-input AND-NOR gate (no power pins)
module _7455_noPower (
  input  _1A,
  input  _1C,
  input  _1B,
  input  _1D,
  input  _2A,
  input  _2C,
  input  _2B,
  input  _2D,
  output Y
);

  wire and_1_out, and_2_out;

  and and_1 (and_1_out, _1A, _1B, _1C, _1D);
  and and_2 (and_2_out, _2A, _2B, _2C, _2D);
  nor nor_1 (Y, and_1_out, and_2_out);

  // Notes on the sheet:
  //   Y: pin 8
  //   _1A: pin 1
  //   _1C: pin 3
  //   _1B: pin 2
  //   _1D: pin 4
  //   _2A: pin 10
  //   _2C: pin 12
  //   _2B: pin 11
  //   _2D: pin 13
endmodule
