// Digital circuit 74163_noPower.dig as structural Verilog
// hex synchronous counter (no power pins)
module _74163_noPower (
  input  nPE,
  input  nSR,
  input  CP,
  input  CET,
  input  CEP,
  input  P0,
  input  P1,
  input  P2,
  input  P3,
  output TC,
  output Q0,
  output Q1,
  output Q2,
  output Q3
);

  wire add_1_c_o, and_1_out;
  wire [3:0] add_1_s, multiplexer_1_out, multiplexer_2_out, multiplexer_3_out;

  Add #(.Bits(4)) add_1 (.a({Q3, Q2, Q1, Q0}), .b(4'b0001), .c_i(1'b0), .s(add_1_s), .c_o(add_1_c_o));
  and and_1 (and_1_out, CEP, CET);
  Multiplexer #(.Bits(4)) multiplexer_1 (
    .sel(and_1_out), .in_0({Q3, Q2, Q1, Q0}), .in_1(add_1_s), .out(multiplexer_1_out));
  Multiplexer #(.Bits(4)) multiplexer_2 (
    .sel(nPE), .in_0({P3, P2, P1, P0}), .in_1(multiplexer_1_out), .out(multiplexer_2_out));
  Multiplexer #(.Bits(4)) multiplexer_3 (.sel(nSR), .in_0(4'b0000), .in_1(multiplexer_2_out), .out(multiplexer_3_out));
  and and_2 (TC, add_1_c_o, CET);
  D_FF #(.Bits(4)) Q (.D(multiplexer_3_out), .C(CP), .Q({Q3, Q2, Q1, Q0}));  // open: nQ

  // Notes on the sheet:
  //   nPE: Parallel Enable, pin 9
  //   nSR: Synchronous Reset, pin 1
  //   CP: pin 2
  //   TC: Terminal Count (overflow out), pin 15
  //   CET: Count Enable Trickle (overflow in), pin 10
  //   CEP: Count Enable Parallel, pin 7
  //   P0: pin 3
  //   P1: pin 4
  //   P2: pin 5
  //   P3: pin 6
  //   Q0: pin 14
  //   Q1: pin 13
  //   Q2: pin 12
  //   Q3: pin 11
endmodule
