// Digital circuit 744017_noPower.dig as structural Verilog
// Johnson decade counter with 10 decoded outputs (no power pins)
module _744017_noPower (
  input  nCP1,
  input  CP0,
  input  MR,
  output Q0,
  output Q1,
  output Q2,
  output Q3,
  output Q4,
  output Q5,
  output Q6,
  output Q7,
  output Q8,
  output Q9,
  output nQ5_9
);

  wire and_1_out, and_2_out, d_ff_as_1_nq, d_ff_as_1_q, d_ff_as_2_nq, d_ff_as_2_q, d_ff_as_3_nq, d_ff_as_3_q,
       d_ff_as_4_nq, d_ff_as_4_q, d_ff_as_5_q, not_1_out, or_1_out;

  not not_1 (not_1_out, nCP1);
  and and_1 (and_1_out, not_1_out, CP0);
  nor nor_1 (Q0, d_ff_as_1_q, d_ff_as_5_q);
  nor nor_2 (Q1, d_ff_as_1_nq, d_ff_as_2_q);
  D_FF_AS d_ff_as_1 (.Set(1'b0), .D(nQ5_9), .C(and_1_out), .Clr(MR), .Q(d_ff_as_1_q), .nQ(d_ff_as_1_nq));
  nor nor_3 (Q2, d_ff_as_3_q, d_ff_as_2_nq);
  nor nor_4 (Q3, d_ff_as_3_nq, d_ff_as_4_q);
  or or_1 (or_1_out, d_ff_as_3_q, d_ff_as_1_q);
  D_FF_AS d_ff_as_2 (.Set(1'b0), .D(d_ff_as_1_q), .C(and_1_out), .Clr(MR), .Q(d_ff_as_2_q), .nQ(d_ff_as_2_nq));
  nor nor_5 (Q4, d_ff_as_4_nq, d_ff_as_5_q);
  and and_2 (and_2_out, or_1_out, d_ff_as_2_q);
  nor nor_6 (Q5, nQ5_9, d_ff_as_1_nq);
  D_FF_AS d_ff_as_3 (.Set(1'b0), .D(and_2_out), .C(and_1_out), .Clr(MR), .Q(d_ff_as_3_q), .nQ(d_ff_as_3_nq));
  nor nor_7 (Q6, d_ff_as_2_nq, d_ff_as_1_q);
  D_FF_AS d_ff_as_4 (.Set(1'b0), .D(d_ff_as_3_q), .C(and_1_out), .Clr(MR), .Q(d_ff_as_4_q), .nQ(d_ff_as_4_nq));
  nor nor_8 (Q7, d_ff_as_3_nq, d_ff_as_2_q);
  nor nor_9 (Q8, d_ff_as_3_q, d_ff_as_4_nq);
  D_FF_AS d_ff_as_5 (.Set(1'b0), .D(d_ff_as_4_q), .C(and_1_out), .Clr(MR), .Q(d_ff_as_5_q), .nQ(nQ5_9));
  nor nor_10 (Q9, nQ5_9, d_ff_as_4_q);

  // Notes on the sheet:
  //   nCP1: pin 13
  //   CP0: pin 14
  //   MR: pin 15
  //   Q0: pin 3
  //   Q1: pin 2
  //   Q2: pin 4
  //   Q3: pin 7
  //   Q4: pin 10
  //   Q5: pin 1
  //   Q6: pin 5
  //   Q7: pin 6
  //   Q8: pin 9
  //   Q9: pin 11
  //   nQ5_9: pin 12
endmodule
