// Digital circuit 7490_noPower.dig as structural Verilog
// asynchronous two - five - decimal addition counter (no power pins)
module _7490_noPower (
  input  CKB,
  input  R_0_1,
  input  R_0_2,
  input  R_9_1,
  input  R_9_2,
  input  CKA,
  output Q_A,
  output Q_B,
  output Q_C,
  output Q_D
);

  wire and_1_out, jk_ff_as_4_nq, nand_1_out, nand_2_out, nand_3_out, not_1_out;

  nand nand_1 (nand_1_out, R_9_1, R_9_2);
  not not_1 (not_1_out, 1'b0);
  nand nand_2 (nand_2_out, R_0_1, R_0_2);
  nand nand_3 (nand_3_out, nand_2_out, nand_1_out);
  JK_FF_AS jk_ff_as_1 (
    .Set(~nand_1_out), .J(not_1_out), .C(~CKA), .K(not_1_out), .Clr(~nand_2_out), .Q(Q_A));  // open: nQ
  JK_FF_AS jk_ff_as_2 (.Set(1'b0), .J(jk_ff_as_4_nq), .C(~CKB), .K(not_1_out), .Clr(nand_3_out), .Q(Q_B));  // open: nQ
  JK_FF_AS jk_ff_as_3 (.Set(1'b0), .J(not_1_out), .C(~Q_B), .K(not_1_out), .Clr(nand_3_out), .Q(Q_C));  // open: nQ
  JK_FF_AS jk_ff_as_4 (
    .Set(~nand_1_out), .J(and_1_out), .C(~CKB), .K(Q_D), .Clr(~nand_2_out), .Q(Q_D), .nQ(jk_ff_as_4_nq));
  and and_1 (and_1_out, Q_B, Q_C);

  // Notes on the sheet:
  //   Q_A: pin 12
  //   Q_B: pin 9
  //   Q_C: pin 8
  //   Q_D: pin 11
  //   CKB: pin 1
  //   R_0_1: pin 2
  //   R_0_2: pin 3
  //   R_9_1: pin 6
  //   R_9_2: pin 7
  //   CKA: pin 14
endmodule
