// Digital circuit 74125_noPower.dig as structural Verilog
// Quadruple bus buffer gates with 3-state outputs (active low output enable) (no power pins)
module _74125_noPower (
  input  A1,
  input  A2,
  input  A3,
  input  A4,
  input  nG1,
  input  nG2,
  input  nG3,
  input  nG4,
  output Y1,
  output Y2,
  output Y3,
  output Y4
);

  wire not_1_out, not_2_out, not_3_out, not_4_out;

  not not_1 (not_1_out, nG1);
  not not_2 (not_2_out, nG2);
  not not_3 (not_3_out, nG3);
  not not_4 (not_4_out, nG4);
  assign Y1 = not_1_out ? A1 : 1'bz;  // Driver driver_1
  assign Y2 = not_2_out ? A2 : 1'bz;  // Driver driver_2
  assign Y3 = not_3_out ? A3 : 1'bz;  // Driver driver_3
  assign Y4 = not_4_out ? A4 : 1'bz;  // Driver driver_4

  // Notes on the sheet:
  //   A1: pin 2
  //   A2: pin 5
  //   A3: pin 9
  //   A4: pin 12
  //   nG1: pin 1, default 1
  //   nG2: pin 4, default 1
  //   nG3: pin 10, default 1
  //   nG4: pin 13, default 1
  //   Y1: pin 3
  //   Y2: pin 6
  //   Y3: pin 8
  //   Y4: pin 11
endmodule
