// Digital circuit 74126_noPower.dig as structural Verilog
// Quadruple bus buffer gates with 3-state outputs (active high output enable) (no power pins)
module _74126_noPower (
  input  A1,
  input  A2,
  input  A3,
  input  A4,
  input  G1,
  input  G2,
  input  G3,
  input  G4,
  output Y1,
  output Y2,
  output Y3,
  output Y4
);

  assign Y1 = G1 ? A1 : 1'bz;  // Driver driver_1
  assign Y2 = G2 ? A2 : 1'bz;  // Driver driver_2
  assign Y3 = G3 ? A3 : 1'bz;  // Driver driver_3
  assign Y4 = G4 ? A4 : 1'bz;  // Driver driver_4

  // Notes on the sheet:
  //   A1: pin 2
  //   A2: pin 5
  //   A3: pin 9
  //   A4: pin 12
  //   G1: pin 1
  //   G2: pin 4
  //   G3: pin 10
  //   G4: pin 13
  //   Y1: pin 3
  //   Y2: pin 6
  //   Y3: pin 8
  //   Y4: pin 11
endmodule
