// Digital circuit 74109_noPower.dig as structural Verilog
// Dual J-NOT-K flip-flop with set and reset; positive-edge-trigger (no power pins)
module _74109_noPower (
  input  _1J,
  input  n1RD,
  input  _1CP,
  input  n1SD,
  input  n1K,
  input  _2J,
  input  n2RD,
  input  _2CP,
  input  n2SD,
  input  n2K,
  output _1Q,
  output n1Q,
  output _2Q,
  output n2Q
);

  wire and_1_out, and_2_out, jk_ff_as_1_nq, jk_ff_as_2_nq;

  JK_FF_AS jk_ff_as_1 (.Set(~n1SD), .J(_1J), .C(_1CP), .K(~n1K), .Clr(~n1RD), .Q(_1Q), .nQ(jk_ff_as_1_nq));
  JK_FF_AS jk_ff_as_2 (.Set(~n2SD), .J(_2J), .C(_2CP), .K(~n2K), .Clr(~n2RD), .Q(_2Q), .nQ(jk_ff_as_2_nq));
  and and_1 (and_1_out, ~n1SD, ~n1RD);  // And
  and and_2 (and_2_out, ~n2SD, ~n2RD);  // And
  or or_1 (n1Q, jk_ff_as_1_nq, and_1_out);
  or or_2 (n2Q, jk_ff_as_2_nq, and_2_out);

  // Notes on the sheet:
  //   _1J: pin 2
  //   n1RD: pin 1
  //   _1CP: pin 4
  //   _1Q: pin 6
  //   n1Q: pin 7
  //   n1SD: pin 5
  //   n1K: pin 3
  //   _2J: pin 14
  //   n2RD: pin 15
  //   _2CP: pin 12
  //   n2SD: pin 11
  //   n2K: pin 13
  //   _2Q: pin 10
  //   n2Q: pin 9
endmodule
