// Digital circuit 7476_noPower.dig as structural Verilog
// dual J-K flip-flops with preset and clear (no power pins)
module _7476_noPower (
  input  _1J,
  input  _1nCLK,
  input  _1K,
  input  _1nC,
  input  _1nS,
  input  _2J,
  input  _2nCLK,
  input  _2K,
  input  _2nC,
  input  _2nS,
  output _1Q,
  output _1nQ,
  output _2Q,
  output _2nQ
);

  wire and_1_out, and_2_out, jk_ff_as_1_nq, jk_ff_as_2_nq;

  JK_FF_AS jk_ff_as_1 (.Set(~_1nS), .J(_1J), .C(~_1nCLK), .K(_1K), .Clr(~_1nC), .Q(_1Q), .nQ(jk_ff_as_1_nq));
  JK_FF_AS jk_ff_as_2 (.Set(~_2nS), .J(_2J), .C(~_2nCLK), .K(_2K), .Clr(~_2nC), .Q(_2Q), .nQ(jk_ff_as_2_nq));
  and and_1 (and_1_out, ~_1nS, ~_1nC);  // And
  and and_2 (and_2_out, ~_2nS, ~_2nC);  // And
  or or_1 (_1nQ, jk_ff_as_1_nq, and_1_out);
  or or_2 (_2nQ, jk_ff_as_2_nq, and_2_out);

  // Notes on the sheet:
  //   _1J: Set, pin 4
  //   _1Q: pin 15
  //   _1nQ: pin 14
  //   _1nCLK: Clock, pin 1
  //   _1K: Kill, pin 16
  //   _1nC: not clear, pin 3
  //   _1nS: not set, pin 2
  //   _2J: Set, pin 9
  //   _2Q: pin 11
  //   _2nQ: pin 10
  //   _2nCLK: Clock, pin 6
  //   _2K: Kill, pin 12
  //   _2nC: not clear, pin 8
  //   _2nS: not set, pin 7
endmodule
