// Digital circuit 74137_noPower.dig as structural Verilog
// 3-to-8 line decoder/demultiplexer, address latch, inverting outputs (no power pins)
module _74137_noPower (
  input  S0,
  input  S1,
  input  S2,
  input  nE1,
  input  E2,
  input  nLE,
  output nY0,
  output nY1,
  output nY2,
  output nY3,
  output nY4,
  output nY5,
  output nY6,
  output nY7
);

  wire and_1_out, not_1_out;
  wire [2:0] d_ff_1_q, delay_1_out;

  and and_1 (and_1_out, nE1, ~E2);  // And
  D_FF #(.Bits(3)) d_ff_1 (.D({S2, S1, S0}), .C(~nLE), .Q(d_ff_1_q));  // open: nQ
  not not_1 (not_1_out, and_1_out);
  Delay #(.Bits(3)) delay_1 (.in(d_ff_1_q), .out(delay_1_out));
  Demultiplexer #(.Selector_Bits(3), .Default(1)) demultiplexer_1 (
    .sel(delay_1_out), .in(not_1_out), .out_0(nY0), .out_1(nY1), .out_2(nY2), .out_3(nY3), .out_4(nY4),
    .out_5(nY5), .out_6(nY6), .out_7(nY7));

  // Notes on the sheet:
  //   S0: pin 1
  //   S1: pin 2
  //   S2: pin 3
  //   nE1: pin 6
  //   E2: pin 5
  //   nLE: pin 4
  //   nY0: pin 15
  //   nY1: pin 14
  //   nY2: pin 13
  //   nY3: pin 12
  //   nY4: pin 11
  //   nY5: pin 10
  //   nY6: pin 9
  //   nY7: pin 7
endmodule
