// Digital circuit 74138_noPower.dig as structural Verilog
// 3-line to 8-line decoder/demultiplexer, inverted out (no power pins)
module _74138_noPower (
  input  A,
  input  B,
  input  C,
  input  G,
  input  nGB,
  input  nGA,
  output nY0,
  output nY1,
  output nY2,
  output nY3,
  output nY4,
  output nY5,
  output nY6,
  output nY7
);

  wire nand_1_out;
  wire [2:0] delay_1_out;

  nand nand_1 (nand_1_out, G, ~nGB, ~nGA);  // NAnd
  Delay #(.Bits(3)) delay_1 (.in({C, B, A}), .out(delay_1_out));
  Demultiplexer #(.Selector_Bits(3), .Default(1)) demultiplexer_1 (
    .sel(delay_1_out), .in(nand_1_out), .out_0(nY0), .out_1(nY1), .out_2(nY2), .out_3(nY3), .out_4(nY4),
    .out_5(nY5), .out_6(nY6), .out_7(nY7));

  // Notes on the sheet:
  //   A: pin 1
  //   B: pin 2
  //   C: pin 3
  //   G: pin 6
  //   nGB: pin 5
  //   nGA: pin 4
  //   nY0: pin 15
  //   nY1: pin 14
  //   nY2: pin 13
  //   nY3: pin 12
  //   nY4: pin 11
  //   nY5: pin 10
  //   nY6: pin 9
  //   nY7: pin 7
endmodule
