// Digital circuit 74139_noPower.dig as structural Verilog
// dual 2-line to 4-line decoder/demultiplexer (no power pins)
module _74139_noPower (
  input  _1A,
  input  _1B,
  input  n1G,
  input  _2A,
  input  _2B,
  input  n2G,
  output n1Y0,
  output n1Y1,
  output n1Y2,
  output n1Y3,
  output n2Y0,
  output n2Y1,
  output n2Y2,
  output n2Y3
);

  Demultiplexer #(.Selector_Bits(2), .Default(1)) demultiplexer_1 (
    .sel({_1B, _1A}), .in(n1G), .out_0(n1Y0), .out_1(n1Y1), .out_2(n1Y2), .out_3(n1Y3));
  Demultiplexer #(.Selector_Bits(2), .Default(1)) demultiplexer_2 (
    .sel({_2B, _2A}), .in(n2G), .out_0(n2Y0), .out_1(n2Y1), .out_2(n2Y2), .out_3(n2Y3));

  // Notes on the sheet:
  //   _1A: pin 2
  //   _1B: pin 3
  //   n1G: pin 1
  //   n1Y0: pin 4
  //   n1Y1: pin 5
  //   n1Y2: pin 6
  //   n1Y3: pin 7
  //   _2A: pin 14
  //   _2B: pin 13
  //   n2G: pin 15
  //   n2Y0: pin 12
  //   n2Y1: pin 11
  //   n2Y2: pin 10
  //   n2Y3: pin 9
endmodule
