// Digital circuit 74237_noPower.dig as structural Verilog
// 3-to-8 line decoder/demultiplexer, address latch, active high outputs (no power pins)
module _74237_noPower (
  input  S0,
  input  S1,
  input  S2,
  input  nE1,
  input  E2,
  input  nLE,
  output Y0,
  output Y1,
  output Y2,
  output Y3,
  output Y4,
  output Y5,
  output Y6,
  output Y7
);

  wire and_1_out;
  wire [2:0] d_ff_1_q;

  and and_1 (and_1_out, nE1, ~E2);  // And
  D_FF #(.Bits(3)) d_ff_1 (.D({S2, S1, S0}), .C(~nLE), .Q(d_ff_1_q));  // open: nQ
  Demultiplexer #(.Selector_Bits(3)) demultiplexer_1 (
    .sel(d_ff_1_q), .in(and_1_out), .out_0(Y0), .out_1(Y1), .out_2(Y2), .out_3(Y3), .out_4(Y4), .out_5(Y5),
    .out_6(Y6), .out_7(Y7));

  // Notes on the sheet:
  //   S0: pin 1
  //   S1: pin 2
  //   S2: pin 3
  //   nE1: pin 6
  //   E2: pin 5
  //   nLE: pin 4
  //   Y0: pin 15
  //   Y1: pin 14
  //   Y2: pin 13
  //   Y3: pin 12
  //   Y4: pin 11
  //   Y5: pin 10
  //   Y6: pin 9
  //   Y7: pin 7
endmodule
