// Digital circuit 74164_noPower.dig as structural Verilog
// 8-bit parallel-out serial shift register, asynchronous clear (no power pins)
module _74164_noPower (
  input  CP,
  input  DSA,
  input  DSB,
  input  nMR,
  output Q0,
  output Q1,
  output Q2,
  output Q3,
  output Q4,
  output Q5,
  output Q6,
  output Q7
);

  wire and_1_out, not_1_out;

  and and_1 (and_1_out, DSA, DSB);
  not not_1 (not_1_out, nMR);
  D_FF_AS d_ff_as_1 (.Set(1'b0), .D(and_1_out), .C(CP), .Clr(not_1_out), .Q(Q0));  // open: nQ
  D_FF_AS d_ff_as_2 (.Set(1'b0), .D(Q0), .C(CP), .Clr(not_1_out), .Q(Q1));  // open: nQ
  D_FF_AS d_ff_as_3 (.Set(1'b0), .D(Q1), .C(CP), .Clr(not_1_out), .Q(Q2));  // open: nQ
  D_FF_AS d_ff_as_4 (.Set(1'b0), .D(Q2), .C(CP), .Clr(not_1_out), .Q(Q3));  // open: nQ
  D_FF_AS d_ff_as_5 (.Set(1'b0), .D(Q3), .C(CP), .Clr(not_1_out), .Q(Q4));  // open: nQ
  D_FF_AS d_ff_as_6 (.Set(1'b0), .D(Q4), .C(CP), .Clr(not_1_out), .Q(Q5));  // open: nQ
  D_FF_AS d_ff_as_7 (.Set(1'b0), .D(Q5), .C(CP), .Clr(not_1_out), .Q(Q6));  // open: nQ
  D_FF_AS d_ff_as_8 (.Set(1'b0), .D(Q6), .C(CP), .Clr(not_1_out), .Q(Q7));  // open: nQ

  // Notes on the sheet:
  //   CP: pin 8
  //   DSA: pin 1
  //   DSB: pin 2
  //   nMR: pin 9
  //   Q0: pin 3
  //   Q1: pin 4
  //   Q2: pin 5
  //   Q3: pin 6
  //   Q4: pin 10
  //   Q5: pin 11
  //   Q6: pin 12
  //   Q7: pin 13
endmodule
