// Digital circuit 74194_noPower.dig as structural Verilog
// 4-Bit Bidirectional Universal Shift Register (no power pins)
module _74194_noPower (
  input  D0,
  input  D1,
  input  D2,
  input  D3,
  input  S0,
  input  S1,
  input  DSL,
  input  DSR,
  input  nMR,
  input  CLK,
  output Q0,
  output Q1,
  output Q2,
  output Q3
);

  wire multiplexer_1_out, multiplexer_2_out, multiplexer_3_out, multiplexer_4_out, nMR_t;

  not not_1 (nMR_t, nMR);
  Multiplexer #(.Selector_Bits(2)) multiplexer_1 (
    .sel({S1, S0}), .in_0(Q0), .in_1(DSR), .in_2(Q1), .in_3(D0), .out(multiplexer_1_out));
  D_FF_AS d_ff_as_1 (.Set(1'b0), .D(multiplexer_1_out), .C(CLK), .Clr(nMR_t), .Q(Q0));  // open: nQ
  Multiplexer #(.Selector_Bits(2)) multiplexer_2 (
    .sel({S1, S0}), .in_0(Q1), .in_1(Q0), .in_2(Q2), .in_3(D1), .out(multiplexer_2_out));
  D_FF_AS d_ff_as_2 (.Set(1'b0), .D(multiplexer_2_out), .C(CLK), .Clr(nMR_t), .Q(Q1));  // open: nQ
  Multiplexer #(.Selector_Bits(2)) multiplexer_3 (
    .sel({S1, S0}), .in_0(Q2), .in_1(Q1), .in_2(Q3), .in_3(D2), .out(multiplexer_3_out));
  D_FF_AS d_ff_as_3 (.Set(1'b0), .D(multiplexer_3_out), .C(CLK), .Clr(nMR_t), .Q(Q2));  // open: nQ
  Multiplexer #(.Selector_Bits(2)) multiplexer_4 (
    .sel({S1, S0}), .in_0(Q3), .in_1(Q2), .in_2(DSL), .in_3(D3), .out(multiplexer_4_out));
  D_FF_AS d_ff_as_4 (.Set(1'b0), .D(multiplexer_4_out), .C(CLK), .Clr(nMR_t), .Q(Q3));  // open: nQ

  // Other names for the same wires on the sheet: sel[1:0] = {S1, S0}

  // Notes on the sheet:
  //   D0: pin 3
  //   D1: pin 4
  //   D2: pin 5
  //   Q0: pin 15
  //   D3: pin 6
  //   S0: pin 9, default 1
  //   S1: pin 10, default 1
  //   DSL: pin 7
  //   DSR: pin 2
  //   Q1: pin 14
  //   Q2: pin 13
  //   Q3: pin 12
  //   nMR: pin 1, default 1
  //   CLK: pin 11
  //   "Datasheet Pins" test is taken from the "real" implementation 74194real
endmodule
